// Logisim project TallerLogica-Combinatorios2.circ as structural Verilog: 9 circuits, main circuit verificador
module sumador_simple (
  input  a,
  input  b,
  output S,
  output Cout
);

  xor xor_1 (S, a, b);
  and and_1 (Cout, a, b);
endmodule

module sumador_completo (
  input  Cin,
  input  A,
  input  B,
  output S,
  output Cout
);

  wire sumador_simple_1_cout, sumador_simple_1_s, sumador_simple_2_cout;

  sumador_simple sumador_simple_1 (.a(A), .b(B), .S(sumador_simple_1_s), .Cout(sumador_simple_1_cout));
  sumador_simple sumador_simple_2 (.a(Cin), .b(sumador_simple_1_s), .S(S), .Cout(sumador_simple_2_cout));
  or or_1 (Cout, sumador_simple_2_cout, sumador_simple_1_cout);
endmodule

module sumador_4 (
  input  Cin,
  input  [3:0] A,
  input  [3:0] B,
  output [3:0] S,
  output Cout
);

  wire sumador_completo_1_cout, sumador_completo_2_cout, sumador_completo_3_cout;

  sumador_completo sumador_completo_1 (.A(A[0]), .B(B[0]), .Cin(Cin), .S(S[0]), .Cout(sumador_completo_1_cout));
  sumador_completo sumador_completo_2 (
    .A(A[1]), .B(B[1]), .Cin(sumador_completo_1_cout), .S(S[1]), .Cout(sumador_completo_2_cout));
  sumador_completo sumador_completo_3 (
    .A(A[2]), .B(B[2]), .Cin(sumador_completo_2_cout), .S(S[2]), .Cout(sumador_completo_3_cout));
  sumador_completo sumador_completo_4 (.A(A[3]), .B(B[3]), .Cin(sumador_completo_3_cout), .S(S[3]), .Cout(Cout));
  Hex_Digit_Display hex_digit_display_1 (.value(S));  // open: dp
endmodule

module comparador_cero (
  input  [3:0] A,
  output Z
);

  wire not_1_out, not_2_out, not_3_out, not_4_out;

  not not_1 (not_1_out, A[0]);
  not not_2 (not_2_out, A[1]);
  not not_3 (not_3_out, A[2]);
  not not_4 (not_4_out, A[3]);
  and and_1 (Z, not_1_out, not_2_out, not_3_out, not_4_out);
endmodule

module sumador_flags (
  input  Cin,
  input  [3:0] A,
  input  [3:0] B,
  output [3:0] S,
  output N,
  output Z,
  output V,
  output C
);

  wire and_1_out, and_2_out, not_1_out, not_2_out, not_3_out;

  sumador_4 sumador_4_1 (.Cin(Cin), .A(A), .S({N, S[2:0]}), .B(B), .Cout(C));
  not not_1 (not_1_out, N);
  and and_1 (and_1_out, not_1_out, A[3], B[3]);
  not not_2 (not_2_out, A[3]);
  not not_3 (not_3_out, B[3]);
  Hex_Digit_Display hex_digit_display_1 (.value({N, S[2:0]}));  // open: dp
  comparador_cero comparador_cero_1 (.A({N, S[2:0]}), .Z(Z));
  and and_2 (and_2_out, not_2_out, not_3_out, N);
  or or_1 (V, and_1_out, and_2_out);

  assign S[3] = N;

  // Notes on the sheet:
  //   A
  //   B
  //   suma
endmodule

module incrementador_4 (
  input  [3:0] A,
  output [3:0] S
);

  sumador_4 sumador_4_1 (.Cin(1'b0), .A(A), .S(S), .B(4'b0001));  // open: Cout
  Hex_Digit_Display hex_digit_display_1 (.value(S));  // open: dp
endmodule

module inversor_4 (
  input  INV,
  input  [3:0] A,
  output [3:0] S
);

  wire undriven;
  wire [3:0] incrementador_4_1_s, not_1_out;

  not not_1 (not_1_out[0], A[0]);
  not not_2 (not_1_out[1], A[1]);
  not not_3 (not_1_out[2], A[2]);
  not not_4 (not_1_out[3], A[3]);
  incrementador_4 incrementador_4_1 (.A(not_1_out), .S(incrementador_4_1_s));
  Multiplexer #(.width(4), .disabled(0)) multiplexer_1 (
    .in0(A), .in1(incrementador_4_1_s), .out(S), .sel(INV), .en(undriven));
  Hex_Digit_Display hex_digit_display_1 (.value(S));  // open: dp
endmodule

module ALU (
  input  [3:0] A,
  input  [3:0] B,
  input  [1:0] OP,
  output N,
  output Z,
  output [3:0] S,
  output V,
  output C
);

  wire comparador_cero_1_z, comparador_cero_2_z, sumador_flags_1_c, sumador_flags_1_n, sumador_flags_1_v,
       sumador_flags_1_z, sumador_flags_2_c, sumador_flags_2_n, sumador_flags_2_v, sumador_flags_2_z;
  wire [3:0] and_1_out, inversor_4_1_s, or_1_out, sumador_flags_1_s, sumador_flags_2_s;

  inversor_4 inversor_4_1 (.A(B), .INV(1'b1), .S(inversor_4_1_s));
  sumador_flags sumador_flags_1 (
    .A(A), .B(B), .Cin(1'b0), .S(sumador_flags_1_s), .N(sumador_flags_1_n), .Z(sumador_flags_1_z),
    .V(sumador_flags_1_v), .C(sumador_flags_1_c));
  sumador_flags sumador_flags_2 (
    .A(A), .B(inversor_4_1_s), .Cin(1'b0), .S(sumador_flags_2_s), .N(sumador_flags_2_n),
    .Z(sumador_flags_2_z), .V(sumador_flags_2_v), .C(sumador_flags_2_c));
  assign and_1_out = B & A;  // AND_Gate and_1, 4 bits wide
  assign or_1_out = A | B;  // OR_Gate or_1, 4 bits wide
  Hex_Digit_Display hex_digit_display_1 (.value(S));  // open: dp
  Multiplexer #(.select(2), .width(4)) multiplexer_1 (
    .in0(sumador_flags_1_s), .in1(sumador_flags_2_s), .in2(and_1_out), .in3(or_1_out), .out(S), .sel(OP));  // open: en
  comparador_cero comparador_cero_1 (.A(and_1_out), .Z(comparador_cero_1_z));
  comparador_cero comparador_cero_2 (.A(or_1_out), .Z(comparador_cero_2_z));
  Multiplexer #(.select(2)) multiplexer_2 (
    .in0(sumador_flags_1_n), .in1(sumador_flags_2_n), .in2(and_1_out[3]), .in3(or_1_out[3]), .out(N), .sel(OP));  // open: en
  Multiplexer #(.select(2)) multiplexer_3 (
    .in0(sumador_flags_1_c), .in1(sumador_flags_2_c), .in2(1'b0), .in3(1'b0), .out(C), .sel(OP));  // open: en
  Multiplexer #(.select(2)) multiplexer_4 (
    .in0(sumador_flags_1_z), .in1(sumador_flags_2_z), .in2(comparador_cero_1_z), .in3(comparador_cero_2_z),
    .out(Z), .sel(OP));  // open: en
  Multiplexer #(.select(2)) multiplexer_5 (
    .in0(sumador_flags_1_v), .in1(sumador_flags_2_v), .in2(1'b0), .in3(1'b0), .out(V), .sel(OP));  // open: en
endmodule

module verificador (
  output [3:0] a,
  output [3:0] b,
  output [1:0] Op,
  output N,
  output Z,
  output V,
  output C,
  output [3:0] Res,
  output halt
);

  wire clock_1_out;

  Clock clock_1 (.out(clock_1_out));
  Counter #(.width(10), .max('h3ff)) counter_1 (
    .Q({Op, b, a}), .carry(halt), .clk(clock_1_out));  // open: load, D, count, clr
  // ALU alu_1: pin names not known; wires that end beside it: a, b, Op, N, Z, V, C, Res
endmodule
